# Fritzing sketch e2_temperature_twitter (saved by Fritzing 0.9.2b)
breadboards: 1

parts:
  Part2 = Arduino Yun
  LED2 = Adafruit_FLORA_RGB_Smart_Pixel
  R3 = Resistor [tolerance=±5% resistance=10k package=THT]  # not connected
  S3 = Square Pushbutton

nets:
  N1: Part2.D2, S3.leg0
  N2: Part2.D6_PWM, LED2.connector2
  N3: Part2.5V, LED2.connector1
  N4: Part2.GND, LED2.connector3
