# Fritzing sketch e3_fan_test (saved by Fritzing 0.9.2b)
breadboards: 1

parts:
  Part3 = Arduino Yun
  Q7 = Basic FET N-Channel [package="TO220 [THT]"]
  R7 = Resistor [tolerance=±5% resistance=150k package="2512 [SMD]"]
  R8 = Resistor [tolerance=±5% resistance=10k package=THT]  # not connected
  S4 = Square Pushbutton
  M1 = DC Motor

nets:
  N1: Part3.D2, S4.leg0
  N2: Part3.D6_PWM, Q7.gate, R7.Pin_1
  N3: Part3.5V, S4.leg1, M1.pin_2
  N4: Part3.GND, Q7.source, R7.Pin_0
  N5: Q7.drain, M1.pin_1
