# Fritzing sketch e3_fullhouse_home_Yun (saved by Fritzing 0.9.2b)
breadboards: 7

parts:
  Part1 = Arduino Uno (Rev3)
  Q1 = NPN-Transistor [package="TO92 [THT]"]
  L1 = Solenoid
  Q2 = NPN-Transistor [package="TO92 [THT]"]
  L2 = Solenoid
  Q3 = NPN-Transistor [package="TO92 [THT]"]
  M1 = DC Motor
  J1 = Basic Servo
  J2 = Basic Servo
  U2 = TMP36 [package=to-92]
  R1 = Resistor [tolerance=±5% resistance=1k package="2512 [SMD]"]
  R2 = Resistor [tolerance=±5% resistance=1k package="2512 [SMD]"]
  R3 = Resistor [tolerance=±5% resistance=1k package="2512 [SMD]"]

nets:
  N1: Part1.A0, U2.VOUT
  N2: Part1.D9_PWM, R2.Pin_0
  N3: Part1.D10_PWM/SS, R3.Pin_0
  N4: Part1.D3_PWM, J2.pulse
  N5: Part1.D4, J1.pulse
  N6: Part1.D6_PWM, R1.Pin_0
  VCC: Part1.5V, L1.pin2, L2.pin2, M1.pin_2, J1.vcc, J2.vcc, U2.VCC
  GND: Part1.GND, Q1.E, Q2.E, Q3.E, J1.gnd, J2.gnd, U2.GND
  N7: Q1.B, R3.Pin_1
  N8: Q1.C, L1.pin1
  N9: Q2.B, R2.Pin_1
  N10: Q2.C, L2.pin1
  N11: Q3.B, R1.Pin_1
  N12: Q3.C, M1.pin_1

notes:
  solenoid
  water plant
  solenoid
  vent room
  DC motor
  turn on fan
  continuous servo
  Down shades
  mirco servo
  pull in clothesline
  temperature sensor
