# Fritzing sketch e3_watering_test (saved by Fritzing 0.9.2b)
breadboards: 1

parts:
  R2 = Resistor [tolerance=±5% resistance=10k package=THT]  # not connected
  S2 = Square Pushbutton
  Part1 = Arduino Yun
  R4 = Resistor [tolerance=±5% resistance=150k package="2512 [SMD]"]
  L2 = Solenoid
  Q5 = Basic FET N-Channel [package="TO220 [THT]"]

nets:
  N1: S2.leg0, Part1.D2
  N2: S2.leg1, Part1.5V, L2.pin2
  N3: Part1.D10_PWM/SS, R4.Pin_1, Q5.gate
  N4: Part1.GND, R4.Pin_0, Q5.source
  N5: L2.pin1, Q5.drain
